# Fritzing sketch main (saved by Fritzing 0.9.2b)
breadboards: 1

parts:
  Raspberry_Pi_1 = Raspberry Pi 3 [part_number=RPI-3-V1.2]
  باجه_۱ = LEDs [package=led10mm]
  باجه2 = LEDs [package=led10mm]
  باجه_3 = LEDs [package=led10mm]
  S1 = Round Pushbutton
  S2 = Round Pushbutton
  S3 = Round Pushbutton
  S4 = Round Pushbutton
  R1 = Resistor [tolerance=±5% resistance=1 package=THT]
  R2 = Resistor [tolerance=±5% resistance=1 package=THT]
  روشن_بودن_دستگاه = LEDs [package=led10mm]
  S5 = Round Pushbutton

nets:
  3V3: Raspberry_Pi_1.3v3, Raspberry_Pi_1.3V3, R1.Pin_1
  N1: Raspberry_Pi_1.GPIO2, باجه_۱.A
  N2: Raspberry_Pi_1.GPIO3, باجه2.A
  N3: Raspberry_Pi_1.GIPO4, باجه_3.A
  N4: Raspberry_Pi_1.GIPO5, S1.leg0
  N5: Raspberry_Pi_1.GIPO6, S2.leg0
  N6: Raspberry_Pi_1.GIPO13, S3.leg0
  N7: Raspberry_Pi_1.GIPO12, S4.leg0
  N8: Raspberry_Pi_1.5V, R2.Pin_1
  N9: باجه_۱.C, R1.Pin_0
  GND: باجه2.C, باجه_3.C, S1.leg1, S2.leg1, S3.leg1, S4.leg1, S5.leg1
  N10: روشن_بودن_دستگاه.C, S5.leg0
